# Fritzing sketch FSR (saved by Fritzing 0.8.5b)
breadboards: 2

parts:
  J1 = Basic Force Sensing Resistor (FSR) [package=THT]
  R1 = Resistor [tolerance=±5% resistance=220 package=THT]
  LCD1 = LCD screen
  R2 = Resistor [tolerance=±5% resistance=220 package=THT]
  R3 = Trimmer Potentiometer [maximum_resistance=10kΩ package=THT]
  パーツ1 = Arduino Uno (Rev3)

nets:
  N1: J1.pin_0, LCD1.VDD, LCD1.V0, LCD1.DB0, R3.leg1
  N2: J1.pin_1, R1.Pin_0, パーツ1.A1
  N3: R1.Pin_1, LCD1.RS, R2.Pin_1, R3.leg2
  N4: LCD1.VSS, R2.Pin_0
  N5: LCD1.R/W, R3.wiper
  N6: LCD1.E, パーツ1.D12/MISO
  N7: LCD1.DB1, パーツ1.D11_PWM/MOSI
  N8: LCD1.DB6, パーツ1.D5_PWM
  N9: LCD1.DB7, パーツ1.D4
  N10: LCD1.LED+, パーツ1.D3_PWM
  N11: LCD1.LED-, パーツ1.D2
